# Fritzing sketch HowToConnect (saved by Fritzing 0.8.7b)

parts:
  Netduino1 = Netduino Plus
  R1 = Resistor [tolerance=±5% resistance=220 package=THT]
  LED1 = LEDs [package=led10mm]

nets:
  N1: Netduino1.D11_MOSI, R1.Pin_0
  N2: Netduino1.GND, LED1.C
  N3: R1.Pin_1, LED1.A
